// Digital circuit DigitalAlarm.dig as structural Verilog
module DigitalAlarm (
  input  CLK,
  input  INC,
  input  SET,
  input  CLR,
  output [6:0] SEC_SEG_1,
  output [6:0] SEC_SEG_2,
  output [6:0] MIN_SEG_1,
  output [6:0] MIN_SEG_2,
  output [6:0] HR_SEG_1,
  output [6:0] HR_SEG_2
);

  wire and_1_out, and_2_out, or_1_out;
  wire [4:0] clockdev_1_hour;
  wire [5:0] clockdev_1_min, clockdev_1_sec;

  and and_1 (and_1_out, CLK, ~SET);  // And
  and and_2 (and_2_out, SET, INC);
  or or_1 (or_1_out, and_1_out, and_2_out);
  ClockDev clockdev_1 (
    .EN(1'b1), .CLR(CLR), .CLK(or_1_out), .SEC(clockdev_1_sec), .MIN(clockdev_1_min), .HOUR(clockdev_1_hour));
  SevenSegmentDecoder sevensegmentdecoder_1 (
    .IN_0(clockdev_1_sec[0]), .IN_1(clockdev_1_sec[1]), .IN_2(clockdev_1_sec[2]), .IN_3(clockdev_1_sec[3]),
    .A(SEC_SEG_1[0]), .B(SEC_SEG_1[1]), .C(SEC_SEG_1[2]), .D(SEC_SEG_1[3]), .E(SEC_SEG_1[4]),
    .F(SEC_SEG_1[5]), .G(SEC_SEG_1[6]));
  SevenSegmentDecoder sevensegmentdecoder_2 (
    .IN_0(clockdev_1_sec[3]), .IN_1(clockdev_1_sec[4]), .IN_2(clockdev_1_sec[5]), .IN_3(1'b0),
    .A(SEC_SEG_2[0]), .B(SEC_SEG_2[1]), .C(SEC_SEG_2[2]), .D(SEC_SEG_2[3]), .E(SEC_SEG_2[4]),
    .F(SEC_SEG_2[5]), .G(SEC_SEG_2[6]));
  SevenSegmentDecoder sevensegmentdecoder_3 (
    .IN_0(clockdev_1_min[0]), .IN_1(clockdev_1_min[1]), .IN_2(clockdev_1_min[2]), .IN_3(clockdev_1_min[3]),
    .A(MIN_SEG_1[0]), .B(MIN_SEG_1[1]), .C(MIN_SEG_1[2]), .D(MIN_SEG_1[3]), .E(MIN_SEG_1[4]),
    .F(MIN_SEG_1[5]), .G(MIN_SEG_1[6]));
  SevenSegmentDecoder sevensegmentdecoder_4 (
    .IN_0(clockdev_1_min[3]), .IN_1(clockdev_1_min[4]), .IN_2(clockdev_1_min[5]), .IN_3(1'b0),
    .A(MIN_SEG_2[0]), .B(MIN_SEG_2[1]), .C(MIN_SEG_2[2]), .D(MIN_SEG_2[3]), .E(MIN_SEG_2[4]),
    .F(MIN_SEG_2[5]), .G(MIN_SEG_2[6]));
  SevenSegmentDecoder sevensegmentdecoder_5 (
    .IN_0(clockdev_1_hour[0]), .IN_1(clockdev_1_hour[1]), .IN_2(clockdev_1_hour[2]),
    .IN_3(clockdev_1_hour[3]), .A(HR_SEG_1[0]), .B(HR_SEG_1[1]), .C(HR_SEG_1[2]), .D(HR_SEG_1[3]),
    .E(HR_SEG_1[4]), .F(HR_SEG_1[5]), .G(HR_SEG_1[6]));
  SevenSegmentDecoder sevensegmentdecoder_6 (
    .IN_0(clockdev_1_hour[3]), .IN_1(clockdev_1_hour[4]), .IN_2(1'b0), .IN_3(1'b0), .A(HR_SEG_2[0]),
    .B(HR_SEG_2[1]), .C(HR_SEG_2[2]), .D(HR_SEG_2[3]), .E(HR_SEG_2[4]), .F(HR_SEG_2[5]), .G(HR_SEG_2[6]));

  // Notes on the sheet:
  //   CLK: Hz: 100
endmodule
